# Fritzing sketch Untitled Sketch 2 (saved by Fritzing 0.9.10b)

parts:
  Mod1 = Amica NodeMCU DEVKIT 1.0
  U1 = 2-Channel 5v Relay Shield [package=relay-2ch5v10a]
  Mod2 = KY-015 Temperature & Humidity Sensor Module [package="Breakout board"]
  BULB1 = Incandescent light bulb small [package="bulb sm"]
  BULB2 = Incandescent light bulb small [package="bulb sm"]

nets:
  N1: Mod1.pin1, Mod1.pin_26, Mod2.Vin
  N2: Mod1.pin2, Mod1.pin_25, Mod1.pin_29, U1.GND, Mod2.-
  N3: Mod1.pin6, Mod2.S
  N4: Mod1.pin_14, U1.IN2
  N5: Mod1.pin_15, U1.IN1
  N6: Mod1.pin_30, U1.VCC
  N7: U1.K1-On, BULB1.1
  N8: U1.K2-On, BULB2.1

custom parts:
  2-Channel 5v Relay Shield: 2 Channel 5v Relay Shield w. 2x SPD-06VDC-SD-C
  KY-015 Temperature & Humidity Sensor Module: KY-015 temperature and humidity sensor module, provides a low-latency serial interface to measure humidity and temperature.
